# Fritzing sketch dice (saved by Fritzing 0.9.4)
breadboards: 1

parts:
  Part1 = Arduino Ethernet Shield (Rev3)
  LED1 = LED - 5mm [color="Red (633nm)" package="5 mm [THT]"]
  LED5 = LED - 5mm [color="Red (633nm)" package="5 mm [THT]"]
  LED6 = LED - 5mm [color="Red (633nm)" package="5 mm [THT]"]
  LED7 = LED - 5mm [color="Red (633nm)" package="5 mm [THT]"]
  LED8 = LED - 5mm [color="Red (633nm)" package="5 mm [THT]"]
  LED9 = LED - 5mm [color="Red (633nm)" package="5 mm [THT]"]
  S1 = Pushbutton [package="[THT]"]

nets:
  N1: Part1.D2, LED9.anode
  N2: Part1.PWM_D3, LED8.anode
  N3: Part1.SDCS, LED7.anode
  N4: Part1.PWM_D5, LED6.anode
  N5: Part1.PWM_D6, LED5.anode
  N6: Part1.D7, LED1.anode
  N7: Part1.RESET, S1.Pin_1, S1.Pin_2
  N8: Part1.GND, LED1.cathode, LED5.cathode, LED6.cathode, LED7.cathode, LED8.cathode, LED9.cathode, S1.Pin_3, S1.Pin_4

custom parts:
  Arduino Ethernet Shield (Rev3): The Arduino Ethernet Shield allows an Arduino board to connect to the internet. It is based on the Wiznet W5100 ethernet chip (datasheet). The Wiznet W5100 provides a network (IP) stack capable of both TCP and UDP. It supports up to four simultaneous socket connections. Use the Ethernet library to write sketches which connect to the internet using the shield. The ethernet shield connects to an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
